// Logisim project F2.3.5-flow.circ as structural Verilog: 1 circuit, main circuit main
module main (
  input  in_1
);

  wire button_1_out, clock_1_out, d_ff_1_qn, decoder_1_out0, decoder_1_out1, decoder_1_out2, decoder_1_out3,
       xor_1_out;
  wire [1:0] d_ff_1_q;

  Clock clock_1 (.out(clock_1_out));
  Button button_1 (.out(button_1_out));
  D_Flip_Flop d_ff_1 (
    .clk(clock_1_out), .D(d_ff_1_qn), .Q(d_ff_1_q[0]), .Qn(d_ff_1_qn), .en(in_1), .reset(button_1_out));  // open: preset
  D_Flip_Flop d_ff_2 (
    .clk(clock_1_out), .D(xor_1_out), .Q(d_ff_1_q[1]), .en(in_1), .reset(button_1_out));  // open: Qn, preset
  LED led_1 (.in(decoder_1_out0));
  LED led_2 (.in(decoder_1_out1));
  LED led_3 (.in(decoder_1_out2));
  Decoder #(.select(2)) decoder_1 (
    .out0(decoder_1_out0), .out1(decoder_1_out1), .out2(decoder_1_out2), .out3(decoder_1_out3),
    .sel(d_ff_1_q), .en(in_1));
  LED led_4 (.in(decoder_1_out3));
  xor xor_1 (xor_1_out, d_ff_1_q[0], d_ff_1_q[1]);
endmodule
