// Logisim project F3.3.5-xnor-transistor.circ as structural Verilog: 1 circuit, main circuit main
module main (
  input  in_1,
  input  in_2,
  output out_3
);

  wire transistor_1_out;

  Transistor transistor_1 (.in(1'b1), .out(transistor_1_out), .gate(in_1));
  Transistor #(.\type ("n")) transistor_2 (.in(1'b0), .out(transistor_1_out), .gate(in_1));
  Transistor transistor_3 (.in(in_2), .out(out_3), .gate(transistor_1_out));
  Transistor transistor_4 (.in(transistor_1_out), .out(out_3), .gate(in_2));
  Transistor #(.\type ("n")) transistor_5 (.in(in_1), .out(out_3), .gate(in_2));
  Transistor #(.\type ("n"), .gate("br")) transistor_6 (.in(in_2), .out(out_3), .gate(in_1));
endmodule
