// Logisim project F3.5.11-4-1-3bit-mux.circ as structural Verilog: 1 circuit, main circuit main
module main (
  input  in_1,
  input  in_2,
  input  in_3,
  input  in_4,
  input  in_5,
  input  in_6,
  input  in_7,
  input  in_8,
  input  in_9,
  input  in_10,
  input  in_11,
  input  in_12,
  input  in_13,
  input  in_14,
  output out_15,
  output out_16,
  output out_17
);

  wire and_1_out, and_2_out, and_3_out, and_4_out, and_5_out, and_6_out, and_7_out, and_8_out, and_9_out,
       and_10_out, and_11_out, and_12_out, and_13_out, and_14_out, and_15_out, and_16_out, not_1_out,
       not_2_out;

  not not_1 (not_1_out, in_13);
  not not_2 (not_2_out, in_14);
  and and_1 (and_1_out, not_1_out, not_2_out);
  and and_2 (and_2_out, in_13, not_2_out);
  and and_3 (and_3_out, not_1_out, in_14);
  and and_4 (and_4_out, in_13, in_14);
  and and_5 (and_5_out, in_3, and_1_out);
  and and_6 (and_6_out, in_12, and_4_out);
  and and_7 (and_7_out, in_6, and_2_out);
  and and_8 (and_8_out, in_9, and_3_out);
  or or_1 (out_17, and_5_out, and_7_out, and_8_out, and_6_out);
  and and_9 (and_9_out, in_2, and_1_out);
  and and_10 (and_10_out, in_5, and_2_out);
  and and_11 (and_11_out, in_8, and_3_out);
  or or_2 (out_16, and_9_out, and_10_out, and_11_out, and_12_out);
  and and_12 (and_12_out, in_11, and_4_out);
  and and_13 (and_13_out, in_1, and_1_out);
  and and_14 (and_14_out, in_7, and_3_out);
  and and_15 (and_15_out, in_10, and_4_out);
  and and_16 (and_16_out, in_4, and_2_out);
  or or_3 (out_15, and_13_out, and_16_out, and_14_out, and_15_out);
endmodule
