// Logisim project F3.5.12-mux-7-segment.circ as structural Verilog: 3 circuits, main circuit main
module main (
  input  in_1,
  input  in_2,
  input  in_3,
  input  in_4,
  input  in_5
);

  wire [7:0] multiplexer_1_out, n7_segment_1_out_12, n7_segment_hex_1_out_12;

  _7_Segment_Hex u_7_segment_hex_1 (
    .in_1(in_1), .in_2(in_2), .in_3(in_3), .in_4(in_4), .out_5(n7_segment_hex_1_out_12[7]),
    .out_6(n7_segment_hex_1_out_12[6]), .out_7(n7_segment_hex_1_out_12[5]),
    .out_8(n7_segment_hex_1_out_12[4]), .out_9(n7_segment_hex_1_out_12[3]),
    .out_10(n7_segment_hex_1_out_12[2]), .out_11(n7_segment_hex_1_out_12[1]),
    .out_12(n7_segment_hex_1_out_12[0]));
  _7_Segment u_7_segment_1 (
    .in_1(in_1), .in_2(in_2), .in_3(in_3), .in_4(in_4), .out_5(n7_segment_1_out_12[7]),
    .out_6(n7_segment_1_out_12[6]), .out_7(n7_segment_1_out_12[5]), .out_8(n7_segment_1_out_12[4]),
    .out_9(n7_segment_1_out_12[3]), .out_10(n7_segment_1_out_12[2]), .out_11(n7_segment_1_out_12[1]),
    .out_12(n7_segment_1_out_12[0]));
  Multiplexer #(.width(8)) multiplexer_1 (
    .in0(n7_segment_1_out_12), .in1(n7_segment_hex_1_out_12), .out(multiplexer_1_out), .sel(in_5));  // open: en
  _7_Segment_Display u_7_segment_display_1 (
    .g(multiplexer_1_out[7]), .f(multiplexer_1_out[6]), .a(multiplexer_1_out[5]), .b(multiplexer_1_out[4]),
    .e(multiplexer_1_out[0]), .d(multiplexer_1_out[1]), .c(multiplexer_1_out[2]), .dp(multiplexer_1_out[3]));
endmodule

module _7_Segment (
  input  in_1,
  input  in_2,
  input  in_3,
  input  in_4,
  output out_5,
  output out_6,
  output out_7,
  output out_8,
  output out_9,
  output out_10,
  output out_11,
  output out_12
);

  wire decoder_1_out0, decoder_1_out1, decoder_1_out2, decoder_1_out3, decoder_1_out4, decoder_1_out5,
       decoder_1_out6, decoder_1_out7, decoder_1_out8, decoder_1_out9, decoder_1_out10, decoder_1_out11,
       decoder_1_out12, decoder_1_out13, decoder_1_out14, decoder_1_out15;

  Decoder #(.select(4)) decoder_1 (
    .out0(decoder_1_out0), .out1(decoder_1_out1), .out2(decoder_1_out2), .out3(decoder_1_out3),
    .out4(decoder_1_out4), .out5(decoder_1_out5), .out6(decoder_1_out6), .out7(decoder_1_out7),
    .out8(decoder_1_out8), .out9(decoder_1_out9), .out10(decoder_1_out10), .out11(decoder_1_out11),
    .out12(decoder_1_out12), .out13(decoder_1_out13), .out14(decoder_1_out14), .out15(decoder_1_out15),
    .sel({in_4, in_3, in_2, in_1}), .en(1'b1));
  or or_1 (out_5, decoder_1_out2, decoder_1_out3, decoder_1_out4, decoder_1_out5, decoder_1_out6, decoder_1_out8, decoder_1_out9);
  or or_2 (out_6, decoder_1_out0, decoder_1_out4, decoder_1_out5, decoder_1_out6, decoder_1_out8, decoder_1_out9);
  or or_3 (out_7, decoder_1_out0, decoder_1_out2, decoder_1_out3, decoder_1_out5, decoder_1_out6, decoder_1_out7, decoder_1_out8, decoder_1_out9);
  or or_4 (out_8, decoder_1_out0, decoder_1_out1, decoder_1_out2, decoder_1_out3, decoder_1_out4, decoder_1_out7, decoder_1_out8, decoder_1_out9);
  or or_5 (out_9, decoder_1_out10, decoder_1_out11, decoder_1_out12, decoder_1_out13, decoder_1_out14, decoder_1_out15);
  or or_6 (out_10, decoder_1_out0, decoder_1_out1, decoder_1_out3, decoder_1_out4, decoder_1_out5, decoder_1_out6, decoder_1_out7, decoder_1_out8, decoder_1_out9);
  or or_7 (out_11, decoder_1_out0, decoder_1_out2, decoder_1_out3, decoder_1_out5, decoder_1_out6, decoder_1_out8, decoder_1_out9);
  or or_8 (out_12, decoder_1_out0, decoder_1_out2, decoder_1_out6, decoder_1_out8);
endmodule

module _7_Segment_Hex (
  input  in_1,
  input  in_2,
  input  in_3,
  input  in_4,
  output out_5,
  output out_6,
  output out_7,
  output out_8,
  output out_9,
  output out_10,
  output out_11,
  output out_12
);

  wire decoder_1_out0, decoder_1_out1, decoder_1_out2, decoder_1_out3, decoder_1_out4, decoder_1_out5,
       decoder_1_out6, decoder_1_out7, decoder_1_out8, decoder_1_out9, decoder_1_out10, decoder_1_out11,
       decoder_1_out12, decoder_1_out13, decoder_1_out14, decoder_1_out15;

  Decoder #(.select(4)) decoder_1 (
    .out0(decoder_1_out0), .out1(decoder_1_out1), .out2(decoder_1_out2), .out3(decoder_1_out3),
    .out4(decoder_1_out4), .out5(decoder_1_out5), .out6(decoder_1_out6), .out7(decoder_1_out7),
    .out8(decoder_1_out8), .out9(decoder_1_out9), .out10(decoder_1_out10), .out11(decoder_1_out11),
    .out12(decoder_1_out12), .out13(decoder_1_out13), .out14(decoder_1_out14), .out15(decoder_1_out15),
    .sel({in_4, in_3, in_2, in_1}), .en(1'b1));
  or or_1 (out_5, decoder_1_out2, decoder_1_out3, decoder_1_out4, decoder_1_out5, decoder_1_out6, decoder_1_out8, decoder_1_out9, decoder_1_out10, decoder_1_out11, decoder_1_out13, decoder_1_out14, decoder_1_out15);
  or or_2 (out_6, decoder_1_out0, decoder_1_out4, decoder_1_out5, decoder_1_out6, decoder_1_out8, decoder_1_out9, decoder_1_out10, decoder_1_out11, decoder_1_out12, decoder_1_out14, decoder_1_out15);
  or or_3 (out_7, decoder_1_out0, decoder_1_out2, decoder_1_out3, decoder_1_out5, decoder_1_out6, decoder_1_out7, decoder_1_out8, decoder_1_out9, decoder_1_out10, decoder_1_out12, decoder_1_out14, decoder_1_out15);
  or or_4 (out_8, decoder_1_out0, decoder_1_out1, decoder_1_out2, decoder_1_out3, decoder_1_out4, decoder_1_out7, decoder_1_out8, decoder_1_out9, decoder_1_out10, decoder_1_out13);
  or or_5 (out_10, decoder_1_out0, decoder_1_out1, decoder_1_out3, decoder_1_out4, decoder_1_out5, decoder_1_out6, decoder_1_out7, decoder_1_out8, decoder_1_out9, decoder_1_out10, decoder_1_out11, decoder_1_out13);
  or or_6 (out_11, decoder_1_out0, decoder_1_out2, decoder_1_out3, decoder_1_out5, decoder_1_out6, decoder_1_out8, decoder_1_out9, decoder_1_out11, decoder_1_out12, decoder_1_out13, decoder_1_out14);
  or or_7 (out_12, decoder_1_out0, decoder_1_out2, decoder_1_out6, decoder_1_out8, decoder_1_out10, decoder_1_out11, decoder_1_out12, decoder_1_out13, decoder_1_out14, decoder_1_out15);

  assign out_9 = 1'b0;
endmodule
