// Logisim project F3.5.14-add.circ as structural Verilog: 1 circuit, main circuit main
module main (
  input  in_1,
  input  in_2,
  input  in_3,
  output out_4,
  output out_5
);

  wire nand_1_out, nand_2_out, xor_1_out;

  xor xor_1 (xor_1_out, in_2, in_3);
  nand nand_1 (nand_1_out, in_2, in_3);
  xor xor_2 (out_4, in_1, xor_1_out);
  nand nand_2 (nand_2_out, in_1, xor_1_out);
  nand nand_3 (out_5, nand_2_out, nand_1_out);
endmodule
