// Logisim project F3.5.16-4bit-add.circ as structural Verilog: 2 circuits, main circuit main
module main (
  input  in_1,
  input  in_2,
  input  in_3,
  input  in_4,
  input  in_5,
  input  in_6,
  input  in_7,
  input  in_8
);

  wire adder_1_out_5, adder_2_out_5, adder_3_out_5, adder_4_out_5;
  wire [3:0] adder_1_out_4;

  LED led_1 (.in(adder_4_out_5));
  Adder adder_1 (.in_2(in_1), .in_3(in_2), .in_1(1'b0), .out_5(adder_1_out_5), .out_4(adder_1_out_4[0]));
  Adder adder_2 (.in_2(in_3), .in_3(in_4), .in_1(adder_1_out_5), .out_5(adder_2_out_5), .out_4(adder_1_out_4[1]));
  Adder adder_3 (.in_2(in_5), .in_3(in_6), .in_1(adder_2_out_5), .out_5(adder_3_out_5), .out_4(adder_1_out_4[2]));
  Adder adder_4 (.in_2(in_7), .in_3(in_8), .in_1(adder_3_out_5), .out_5(adder_4_out_5), .out_4(adder_1_out_4[3]));
  Hex_Digit_Display hex_digit_display_1 (.value(adder_1_out_4));  // open: dp
endmodule

module Adder (
  input  in_1,
  input  in_2,
  input  in_3,
  output out_4,
  output out_5
);

  wire nand_1_out, nand_2_out, xor_1_out;

  xor xor_1 (xor_1_out, in_2, in_3);
  nand nand_1 (nand_1_out, in_2, in_3);
  xor xor_2 (out_4, in_1, xor_1_out);
  nand nand_2 (nand_2_out, in_1, xor_1_out);
  nand nand_3 (out_5, nand_2_out, nand_1_out);
endmodule
