// Logisim project F3.5.2-2-4-sub.circ as structural Verilog: 2 circuits, main circuit main
module main (
);

  _2_4decoder u_2_4decoder_1 ();  // open: in_1, in_2, out_3, out_4, out_5, out_6
endmodule

module _2_4decoder (
  input  in_1,
  input  in_2,
  output out_3,
  output out_4,
  output out_5,
  output out_6
);

  wire not_1_out, not_2_out;

  not not_1 (not_1_out, in_2);
  not not_2 (not_2_out, in_1);
  and and_1 (out_3, not_2_out, not_1_out);
  and and_2 (out_4, in_1, not_1_out);
  and and_3 (out_5, not_2_out, in_2);
  and and_4 (out_6, in_1, in_2);
endmodule
