// Logisim project F3.5.3-3-8-decoder.circ as structural Verilog: 2 circuits, main circuit main
module main (
  input  in_1,
  input  in_2,
  input  in_3,
  output out_4,
  output out_5,
  output out_6,
  output out_7,
  output out_8,
  output out_9,
  output out_10,
  output out_11
);

  wire not_1_out;

  _2_4decoder u_2_4decoder_1 (
    .in_1(in_1), .in_2(in_2), .in_3(not_1_out), .out_4(out_4), .out_5(out_5), .out_6(out_6), .out_7(out_7));
  not not_1 (not_1_out, in_3);
  _2_4decoder u_2_4decoder_2 (
    .in_1(in_1), .in_2(in_2), .in_3(in_3), .out_4(out_8), .out_5(out_9), .out_6(out_10), .out_7(out_11));
endmodule

module _2_4decoder (
  input  in_1,
  input  in_2,
  input  in_3,
  output out_4,
  output out_5,
  output out_6,
  output out_7
);

  wire not_1_out, not_2_out;

  not not_1 (not_1_out, in_1);
  not not_2 (not_2_out, in_2);
  and and_1 (out_4, not_1_out, in_3, not_2_out);
  and and_2 (out_5, in_1, in_3, not_2_out);
  and and_3 (out_6, not_1_out, in_3, in_2);
  and and_4 (out_7, in_1, in_3, in_2);
endmodule
