// Logisim project F3.5.8-16-4-priority.circ as structural Verilog: 3 circuits, main circuit main
module main (
  input  in_1,
  input  in_2,
  input  in_3,
  input  in_4,
  input  in_5,
  input  in_6,
  input  in_7,
  input  in_8,
  input  in_9,
  input  in_10,
  input  in_11,
  input  in_12,
  input  in_13,
  input  in_14,
  input  in_15,
  input  in_16
);

  wire multiplexer_1_out, multiplexer_2_out, n4_2_priority_encoder_1_out_5, n4_2_priority_encoder_1_out_6,
       n4_2_priority_encoder_3_out_5, n4_2_priority_encoder_3_out_6, n4_2_priority_encoder_4_out_5,
       n4_2_priority_encoder_4_out_6, n4_2_priority_encoder_5_out_5, n4_2_priority_encoder_5_out_6,
       n7_segment_decoder_1_out_5, n7_segment_decoder_1_out_6, n7_segment_decoder_1_out_7,
       n7_segment_decoder_1_out_8, n7_segment_decoder_1_out_9, n7_segment_decoder_1_out_10,
       n7_segment_decoder_1_out_11, or_1_out, or_2_out, or_3_out, or_4_out;
  wire [1:0] n4_2_priority_encoder_2_out_6;

  or or_1 (or_1_out, in_13, in_14, in_15, in_16);
  or or_2 (or_2_out, in_9, in_10, in_11, in_12);
  or or_3 (or_3_out, in_5, in_6, in_7, in_8);
  _4_2_Priority_Encoder u_4_2_priority_encoder_1 (
    .in_1(in_1), .in_2(in_2), .in_3(in_3), .in_4(in_4), .out_5(n4_2_priority_encoder_1_out_5),
    .out_6(n4_2_priority_encoder_1_out_6));
  or or_4 (or_4_out, in_1, in_2, in_3, in_4);
  _4_2_Priority_Encoder u_4_2_priority_encoder_2 (
    .in_1(or_4_out), .in_2(or_3_out), .in_3(or_2_out), .in_4(or_1_out),
    .out_5(n4_2_priority_encoder_2_out_6[1]), .out_6(n4_2_priority_encoder_2_out_6[0]));
  _4_2_Priority_Encoder u_4_2_priority_encoder_3 (
    .in_1(in_5), .in_2(in_6), .in_3(in_7), .in_4(in_8), .out_5(n4_2_priority_encoder_3_out_5),
    .out_6(n4_2_priority_encoder_3_out_6));
  _4_2_Priority_Encoder u_4_2_priority_encoder_4 (
    .in_1(in_9), .in_2(in_10), .in_3(in_11), .in_4(in_12), .out_5(n4_2_priority_encoder_4_out_5),
    .out_6(n4_2_priority_encoder_4_out_6));
  _4_2_Priority_Encoder u_4_2_priority_encoder_5 (
    .in_1(in_13), .in_2(in_14), .in_3(in_15), .in_4(in_16), .out_5(n4_2_priority_encoder_5_out_5),
    .out_6(n4_2_priority_encoder_5_out_6));
  Multiplexer #(.select(2)) multiplexer_1 (
    .in0(n4_2_priority_encoder_1_out_5), .in1(n4_2_priority_encoder_3_out_5),
    .in2(n4_2_priority_encoder_4_out_5), .in3(n4_2_priority_encoder_5_out_5), .out(multiplexer_1_out),
    .sel(n4_2_priority_encoder_2_out_6), .en(1'b1));
  Multiplexer #(.select(2)) multiplexer_2 (
    .in0(n4_2_priority_encoder_1_out_6), .in1(n4_2_priority_encoder_3_out_6),
    .in2(n4_2_priority_encoder_4_out_6), .in3(n4_2_priority_encoder_5_out_6), .out(multiplexer_2_out),
    .sel(n4_2_priority_encoder_2_out_6), .en(1'b1));
  _7_Segment_Decoder u_7_segment_decoder_1 (
    .in_1(multiplexer_2_out), .in_2(multiplexer_1_out), .in_3(n4_2_priority_encoder_2_out_6[0]),
    .in_4(n4_2_priority_encoder_2_out_6[1]), .out_5(n7_segment_decoder_1_out_5),
    .out_6(n7_segment_decoder_1_out_6), .out_7(n7_segment_decoder_1_out_7),
    .out_8(n7_segment_decoder_1_out_8), .out_9(n7_segment_decoder_1_out_9),
    .out_10(n7_segment_decoder_1_out_10), .out_11(n7_segment_decoder_1_out_11));
  _7_Segment_Display u_7_segment_display_1 (
    .g(n7_segment_decoder_1_out_5), .f(n7_segment_decoder_1_out_6), .a(n7_segment_decoder_1_out_7),
    .b(n7_segment_decoder_1_out_8), .e(n7_segment_decoder_1_out_11), .d(n7_segment_decoder_1_out_10),
    .c(n7_segment_decoder_1_out_9));  // open: dp
endmodule

module _7_Segment_Decoder (
  input  in_1,
  input  in_2,
  input  in_3,
  input  in_4,
  output out_5,
  output out_6,
  output out_7,
  output out_8,
  output out_9,
  output out_10,
  output out_11
);

  wire decoder_1_out0, decoder_1_out1, decoder_1_out2, decoder_1_out3, decoder_1_out4, decoder_1_out5,
       decoder_1_out6, decoder_1_out7, decoder_1_out8, decoder_1_out9, decoder_1_out10, decoder_1_out11,
       decoder_1_out12, decoder_1_out13, decoder_1_out14, decoder_1_out15;

  Decoder #(.select(4)) decoder_1 (
    .out0(decoder_1_out0), .out1(decoder_1_out1), .out2(decoder_1_out2), .out3(decoder_1_out3),
    .out4(decoder_1_out4), .out5(decoder_1_out5), .out6(decoder_1_out6), .out7(decoder_1_out7),
    .out8(decoder_1_out8), .out9(decoder_1_out9), .out10(decoder_1_out10), .out11(decoder_1_out11),
    .out12(decoder_1_out12), .out13(decoder_1_out13), .out14(decoder_1_out14), .out15(decoder_1_out15),
    .sel({in_4, in_3, in_2, in_1}), .en(1'b1));
  or or_1 (out_5, decoder_1_out2, decoder_1_out3, decoder_1_out4, decoder_1_out5, decoder_1_out6, decoder_1_out8, decoder_1_out9, decoder_1_out10, decoder_1_out11, decoder_1_out13, decoder_1_out14, decoder_1_out15);
  or or_2 (out_6, decoder_1_out0, decoder_1_out4, decoder_1_out5, decoder_1_out6, decoder_1_out8, decoder_1_out9, decoder_1_out10, decoder_1_out11, decoder_1_out12, decoder_1_out14, decoder_1_out15);
  or or_3 (out_7, decoder_1_out0, decoder_1_out2, decoder_1_out3, decoder_1_out5, decoder_1_out6, decoder_1_out7, decoder_1_out8, decoder_1_out9, decoder_1_out10, decoder_1_out12, decoder_1_out14, decoder_1_out15);
  or or_4 (out_8, decoder_1_out0, decoder_1_out1, decoder_1_out2, decoder_1_out3, decoder_1_out4, decoder_1_out7, decoder_1_out8, decoder_1_out9, decoder_1_out10, decoder_1_out13);
  or or_5 (out_9, decoder_1_out0, decoder_1_out1, decoder_1_out3, decoder_1_out4, decoder_1_out5, decoder_1_out6, decoder_1_out7, decoder_1_out8, decoder_1_out9, decoder_1_out10, decoder_1_out11, decoder_1_out13);
  or or_6 (out_10, decoder_1_out0, decoder_1_out2, decoder_1_out3, decoder_1_out5, decoder_1_out6, decoder_1_out8, decoder_1_out9, decoder_1_out11, decoder_1_out12, decoder_1_out13, decoder_1_out14);
  or or_7 (out_11, decoder_1_out0, decoder_1_out2, decoder_1_out6, decoder_1_out8, decoder_1_out10, decoder_1_out11, decoder_1_out12, decoder_1_out13, decoder_1_out14, decoder_1_out15);
endmodule

module _4_2_Priority_Encoder (
  input  in_1,
  input  in_2,
  input  in_3,
  input  in_4,
  output out_5,
  output out_6
);

  wire nand_2_out, not_1_out, not_2_out;

  not not_1 (not_1_out, in_3);
  not not_2 (not_2_out, in_4);
  nand nand_1 (out_5, not_1_out, not_2_out);
  nand nand_2 (nand_2_out, in_2, not_1_out);
  nand nand_3 (out_6, nand_2_out, not_2_out);
endmodule
