// Logisim project F3.6.1-sub.circ as structural Verilog: 2 circuits, main circuit main
module main (
  input  in_1,
  input  in_2,
  input  in_3,
  input  in_4,
  input  in_5,
  input  in_6,
  input  in_7,
  input  in_8
);

  wire subtractor_1_out_5, subtractor_2_out_5, subtractor_3_out_5, subtractor_4_out_5;
  wire [3:0] subtractor_1_out_4;

  Hex_Digit_Display hex_digit_display_1 (.value({in_8, in_6, in_4, in_2}));  // open: dp
  Hex_Digit_Display hex_digit_display_2 (.value({in_7, in_5, in_3, in_1}));  // open: dp
  Subtractor subtractor_1 (
    .in_2(in_1), .in_3(in_2), .in_1(1'b0), .out_5(subtractor_1_out_5), .out_4(subtractor_1_out_4[0]));
  Subtractor subtractor_2 (
    .in_2(in_3), .in_3(in_4), .in_1(subtractor_1_out_5), .out_5(subtractor_2_out_5),
    .out_4(subtractor_1_out_4[1]));
  Subtractor subtractor_3 (
    .in_2(in_5), .in_3(in_6), .in_1(subtractor_2_out_5), .out_5(subtractor_3_out_5),
    .out_4(subtractor_1_out_4[2]));
  Subtractor subtractor_4 (
    .in_2(in_7), .in_3(in_8), .in_1(subtractor_3_out_5), .out_5(subtractor_4_out_5),
    .out_4(subtractor_1_out_4[3]));
  LED led_1 (.in(subtractor_4_out_5));
  Hex_Digit_Display hex_digit_display_3 (.value(subtractor_1_out_4));  // open: dp
endmodule

module Subtractor (
  input  in_1,
  input  in_2,
  input  in_3,
  output out_4,
  output out_5
);

  wire nand_1_out, nand_2_out, not_1_out, xor_1_out;

  xor xor_1 (xor_1_out, in_2, in_3);
  not not_1 (not_1_out, xor_1_out);
  nand nand_1 (nand_1_out, xor_1_out, in_3);
  xor xor_2 (out_4, in_1, xor_1_out);
  nand nand_2 (nand_2_out, in_1, not_1_out);
  nand nand_3 (out_5, nand_2_out, nand_1_out);
endmodule
