// Logisim project F3.6.2-add-sign.circ as structural Verilog: 3 circuits, main circuit main
module main (
  input  in_1,
  input  in_2,
  input  in_3,
  input  in_4,
  input  in_5,
  input  in_6,
  input  in_7,
  input  in_8
);

  wire adder_1_out_5, adder_2_out_5, adder_3_out_5, subtractor_1_out_5, subtractor_2_out_5,
       subtractor_3_out_5, subtractor_5_out_5, subtractor_6_out_5, xor_1_out;
  wire [2:0] adder_2_out_4, subtractor_3_out_4, subtractor_6_out_4;
  wire [3:0] multiplexer_1_out, multiplexer_2_out;

  xor xor_1 (xor_1_out, in_8, in_7);
  Adder adder_1 (.in_2(in_5), .in_3(in_6), .in_1(adder_3_out_5), .out_5(adder_1_out_5), .out_4(adder_2_out_4[2]));
  LED led_1 (.in(adder_1_out_5));
  Adder adder_2 (.in_2(in_1), .in_3(in_2), .in_1(1'b0), .out_5(adder_2_out_5), .out_4(adder_2_out_4[0]));
  Adder adder_3 (.in_2(in_3), .in_3(in_4), .in_1(adder_2_out_5), .out_5(adder_3_out_5), .out_4(adder_2_out_4[1]));
  Subtractor subtractor_1 (
    .in_2(in_5), .in_3(in_6), .in_1(subtractor_2_out_5), .out_5(subtractor_1_out_5),
    .out_4(subtractor_3_out_4[2]));
  Subtractor subtractor_2 (
    .in_2(in_3), .in_3(in_4), .in_1(subtractor_3_out_5), .out_5(subtractor_2_out_5),
    .out_4(subtractor_3_out_4[1]));
  Multiplexer #(.width(4)) multiplexer_1 (
    .in0({in_8, adder_2_out_4}), .in1(multiplexer_2_out), .out(multiplexer_1_out), .sel(xor_1_out));  // open: en
  Subtractor subtractor_3 (
    .in_2(in_1), .in_3(in_2), .in_1(1'b0), .out_5(subtractor_3_out_5), .out_4(subtractor_3_out_4[0]));
  _7_Segment_Display u_7_segment_display_1 (.g(multiplexer_1_out[3]));  // open: f, a, b, e, d, c, dp
  Subtractor subtractor_4 (
    .in_2(in_6), .in_3(in_5), .in_1(subtractor_5_out_5), .out_4(subtractor_6_out_4[2]));  // open: out_5
  Subtractor subtractor_5 (
    .in_2(in_4), .in_3(in_3), .in_1(subtractor_6_out_5), .out_5(subtractor_5_out_5),
    .out_4(subtractor_6_out_4[1]));
  Multiplexer #(.width(4)) multiplexer_2 (
    .in0({in_7, subtractor_3_out_4}), .in1({in_8, subtractor_6_out_4}), .out(multiplexer_2_out),
    .sel(subtractor_1_out_5));  // open: en
  Hex_Digit_Display hex_digit_display_1 (.value({1'b0, multiplexer_1_out[2:0]}));  // open: dp
  Subtractor subtractor_6 (
    .in_2(in_2), .in_3(in_1), .in_1(1'b0), .out_5(subtractor_6_out_5), .out_4(subtractor_6_out_4[0]));

  // Notes on the sheet:
  //   A+B
  //   A-B
  //   B-A
endmodule

module Adder (
  input  in_1,
  input  in_2,
  input  in_3,
  output out_4,
  output out_5
);

  wire nand_1_out, nand_2_out, xor_1_out;

  xor xor_1 (xor_1_out, in_2, in_3);
  nand nand_1 (nand_1_out, in_2, in_3);
  xor xor_2 (out_4, in_1, xor_1_out);
  nand nand_2 (nand_2_out, in_1, xor_1_out);
  nand nand_3 (out_5, nand_2_out, nand_1_out);
endmodule

module Subtractor (
  input  in_1,
  input  in_2,
  input  in_3,
  output out_4,
  output out_5
);

  wire nand_1_out, nand_2_out, not_1_out, xor_1_out;

  xor xor_1 (xor_1_out, in_2, in_3);
  not not_1 (not_1_out, xor_1_out);
  nand nand_1 (nand_1_out, xor_1_out, in_3);
  xor xor_2 (out_4, in_1, xor_1_out);
  nand nand_2 (nand_2_out, in_1, not_1_out);
  nand nand_3 (out_5, nand_2_out, nand_1_out);
endmodule
