// Logisim project F3.6.3-add-one's.circ as structural Verilog: 4 circuits, main circuit main
module main (
  input  in_1,
  input  in_2,
  input  in_3,
  input  in_4,
  input  in_5,
  input  in_6,
  input  in_7,
  input  in_8,
  output out_9,
  output out_10,
  output out_11,
  output out_12
);

  wire [2:0] adder_sign_1_out_9, multiplexer_1_out, multiplexer_2_out, not_1_out, not_4_out, not_7_out;

  not not_1 (not_1_out[0], in_1);
  not not_2 (not_1_out[1], in_2);
  not not_3 (not_1_out[2], in_3);
  not not_4 (not_4_out[0], in_5);
  not not_5 (not_4_out[1], in_6);
  not not_6 (not_4_out[2], in_7);
  Multiplexer #(.width(3)) multiplexer_1 (
    .in0({in_7, in_6, in_5}), .in1(not_4_out), .out(multiplexer_1_out), .sel(in_8));  // open: en
  Multiplexer #(.width(3)) multiplexer_2 (
    .in0({in_3, in_2, in_1}), .in1(not_1_out), .out(multiplexer_2_out), .sel(in_4));  // open: en
  Adder_Sign adder_sign_1 (
    .in_1(multiplexer_2_out[0]), .in_2(multiplexer_1_out[0]), .in_3(multiplexer_2_out[1]),
    .in_4(multiplexer_1_out[1]), .in_5(multiplexer_2_out[2]), .in_6(multiplexer_1_out[2]), .in_7(in_4),
    .in_8(in_8), .out_9({out_12, adder_sign_1_out_9}));
  not not_7 (not_7_out[0], adder_sign_1_out_9[0]);
  not not_8 (not_7_out[1], adder_sign_1_out_9[1]);
  not not_9 (not_7_out[2], adder_sign_1_out_9[2]);
  Multiplexer #(.width(3)) multiplexer_3 (
    .in0(adder_sign_1_out_9), .in1(not_7_out), .out({out_11, out_10, out_9}), .sel(out_12));  // open: en
endmodule

module Adder (
  input  in_1,
  input  in_2,
  input  in_3,
  output out_4,
  output out_5
);

  wire nand_1_out, nand_2_out, xor_1_out;

  xor xor_1 (xor_1_out, in_2, in_3);
  nand nand_1 (nand_1_out, in_2, in_3);
  xor xor_2 (out_4, in_1, xor_1_out);
  nand nand_2 (nand_2_out, in_1, xor_1_out);
  nand nand_3 (out_5, nand_2_out, nand_1_out);
endmodule

module Subtractor (
  input  in_1,
  input  in_2,
  input  in_3,
  output out_4,
  output out_5
);

  wire nand_1_out, nand_2_out, not_1_out, xor_1_out;

  xor xor_1 (xor_1_out, in_2, in_3);
  not not_1 (not_1_out, xor_1_out);
  nand nand_1 (nand_1_out, xor_1_out, in_3);
  xor xor_2 (out_4, in_1, xor_1_out);
  nand nand_2 (nand_2_out, in_1, not_1_out);
  nand nand_3 (out_5, nand_2_out, nand_1_out);
endmodule

module Adder_Sign (
  input  in_1,
  input  in_2,
  input  in_3,
  input  in_4,
  input  in_5,
  input  in_6,
  input  in_7,
  input  in_8,
  output [3:0] out_9
);

  wire adder_1_out_5, adder_2_out_5, adder_3_out_5, subtractor_1_out_5, subtractor_2_out_5,
       subtractor_3_out_5, subtractor_5_out_5, subtractor_6_out_5, xor_1_out;
  wire [2:0] adder_3_out_4, subtractor_3_out_4, subtractor_6_out_4;
  wire [3:0] multiplexer_2_out;

  xor xor_1 (xor_1_out, in_8, in_7);
  Adder adder_1 (.in_2(in_5), .in_3(in_6), .in_1(adder_2_out_5), .out_5(adder_1_out_5), .out_4(adder_3_out_4[2]));
  LED led_1 (.in(adder_1_out_5));
  Adder adder_2 (.in_2(in_3), .in_3(in_4), .in_1(adder_3_out_5), .out_5(adder_2_out_5), .out_4(adder_3_out_4[1]));
  Adder adder_3 (.in_2(in_1), .in_3(in_2), .in_1(1'b0), .out_5(adder_3_out_5), .out_4(adder_3_out_4[0]));
  Subtractor subtractor_1 (
    .in_2(in_5), .in_3(in_6), .in_1(subtractor_2_out_5), .out_5(subtractor_1_out_5),
    .out_4(subtractor_3_out_4[2]));
  Subtractor subtractor_2 (
    .in_2(in_3), .in_3(in_4), .in_1(subtractor_3_out_5), .out_5(subtractor_2_out_5),
    .out_4(subtractor_3_out_4[1]));
  Multiplexer #(.width(4)) multiplexer_1 (
    .in0({in_8, adder_3_out_4}), .in1(multiplexer_2_out), .out(out_9), .sel(xor_1_out));  // open: en
  Subtractor subtractor_3 (
    .in_2(in_1), .in_3(in_2), .in_1(1'b0), .out_5(subtractor_3_out_5), .out_4(subtractor_3_out_4[0]));
  Subtractor subtractor_4 (
    .in_2(in_6), .in_3(in_5), .in_1(subtractor_5_out_5), .out_4(subtractor_6_out_4[2]));  // open: out_5
  Subtractor subtractor_5 (
    .in_2(in_4), .in_3(in_3), .in_1(subtractor_6_out_5), .out_5(subtractor_5_out_5),
    .out_4(subtractor_6_out_4[1]));
  Multiplexer #(.width(4)) multiplexer_2 (
    .in0({in_7, subtractor_3_out_4}), .in1({in_8, subtractor_6_out_4}), .out(multiplexer_2_out),
    .sel(subtractor_1_out_5));  // open: en
  Subtractor subtractor_6 (
    .in_2(in_2), .in_3(in_1), .in_1(1'b0), .out_5(subtractor_6_out_5), .out_4(subtractor_6_out_4[0]));

  // Notes on the sheet:
  //   A+B
  //   A-B
  //   B-A
endmodule
